# Fritzing sketch Hovercraft (saved by Fritzing 0.9.3b)
breadboards: 1

parts:
  Part1 = Arduino Uno (Rev3)
  Part2 = Bluetooth HC-05 Macho
  J1 = Basic Servo
  J2 = Basic Servo

nets:
  N1: Part1.D2, Part2.TXD
  N2: Part1.D3_PWM, Part2.RXD
  N3: Part1.D4, J1.pulse
  N4: Part1.D5_PWM, J2.pulse
  VCC: Part1.5V, Part2.VCC, J1.vcc
  GND: Part1.GND, Part2.GND, J1.gnd, J2.gnd

notes:
  backServo
  bottomServo
  Model Airplane Battery
